// Digital circuit frontpanel.dig as structural Verilog
module frontpanel (
  output [31:0] R0,
  output [31:0] R1,
  output [31:0] R2,
  output [31:0] R3,
  output [3:0] PC
);

  wire add, advance_out, decoder_1_p1, decoder_1_p2, fetch_1_p6, hex, hexdisplay_1_p2, hexdisplay_1_p4,
       hexdisplay_1_p6, hexdisplay_1_p7, hexdisplay_1_p9, hexdisplay_1_p11, hexdisplay_1_p14,
       hexdisplay_1_p16, hexdisplay_2_p2, hexdisplay_2_p4, hexdisplay_2_p7, hexdisplay_2_p9,
       hexdisplay_2_p11, hexdisplay_2_p14, hexdisplay_2_p16, instrdisplay_1_p1, instrdisplay_1_p3,
       instrdisplay_1_p5, instrdisplay_1_p7, instrdisplay_1_p9, instrdisplay_1_p11, instrdisplay_1_p14,
       instrdisplay_1_p16, instrdisplay_1_p18, jump, move, op, pmshim_1_c, pmshim_1_l, pmshim_1_s,
       regdisplay_1_p1, regdisplay_1_p2, regdisplay_2_p1, regdisplay_2_p3, regdisplay_2_p5, regdisplay_2_p8,
       regdisplay_2_p12, rs, tworeg;
  wire [1:0] rd;
  wire [2:0] R;
  wire [3:0] hexdisplay_1_p1, hexdisplay_1_p3, hexdisplay_1_p5, hexdisplay_1_p8, hexdisplay_1_p10,
       hexdisplay_1_p13, hexdisplay_1_p15, hexdisplay_1_p17, hexdisplay_2_p1, hexdisplay_2_p3,
       hexdisplay_2_p5, hexdisplay_2_p8, hexdisplay_2_p10, hexdisplay_2_p13, hexdisplay_2_p15,
       hexdisplay_2_p17, instrdisplay_1_p2, instrdisplay_1_p4, pmshim_1_a, regdisplay_2_p2, regdisplay_2_p4;
  wire [15:0] decoder_1_p6, execute_1_r_out, instrdisplay_1_p6, instrdisplay_1_p8, instrdisplay_1_p10,
       instrdisplay_1_p13, instrdisplay_1_p15, instrdisplay_1_p17, L, pmshim_1_d, Program_d, regdisplay_1_d1,
       regdisplay_1_d2, regdisplay_2_p6, regdisplay_2_p10;

  SixteenSeg sixteenseg_1 (.led(regdisplay_1_d1), .dp(regdisplay_1_p1));
  regdisplay regdisplay_1 (
    .D1(regdisplay_1_d1), .P1(regdisplay_1_p1), .D2(regdisplay_1_d2), .P2(regdisplay_1_p2), .E(1'b1),
    .J(jump), .R(rd));
  SixteenSeg sixteenseg_2 (.led(regdisplay_1_d2), .dp(regdisplay_1_p2));
  pmshim pmshim_1 (.pc(PC), .A(pmshim_1_a), .D(pmshim_1_d), .s(pmshim_1_s), .C(pmshim_1_c), .L(pmshim_1_l));
  Seven_Seg_Hex seven_seg_hex_1 (.d(hexdisplay_1_p1), .dp(hexdisplay_1_p2));
  Seven_Seg_Hex seven_seg_hex_2 (.d(hexdisplay_1_p3), .dp(hexdisplay_1_p4));
  // hexdisplay hexdisplay_1: pin names not known; wires that end beside it: hexdisplay_1_p1, hexdisplay_1_p2, hexdisplay_1_p3, hexdisplay_1_p4, hexdisplay_1_p5, hexdisplay_1_p6, hexdisplay_1_p7, hexdisplay_1_p8, hexdisplay_1_p9, hexdisplay_1_p10, hexdisplay_1_p11, L, hexdisplay_1_p13, hexdisplay_1_p14, hexdisplay_1_p15, hexdisplay_1_p16, hexdisplay_1_p17, hex
  not not_1 (hexdisplay_1_p6, jump);
  EEPROMDualPort #(.AddrBits(4), .isProgramMemory("true"), .Bits(16)) Program (
    .A(pmshim_1_a), .Din(pmshim_1_d), .str(pmshim_1_s), .C(pmshim_1_c), .ld(pmshim_1_l), .D(Program_d));
  Button advance (.out(advance_out));
  Seven_Seg_Hex seven_seg_hex_3 (.d(hexdisplay_1_p5), .dp(hexdisplay_1_p7));
  Seven_Seg_Hex seven_seg_hex_4 (.d(hexdisplay_1_p8), .dp(hexdisplay_1_p9));
  Seven_Seg_Hex seven_seg_hex_5 (.d(hexdisplay_1_p10), .dp(hexdisplay_1_p11));
  Seven_Seg_Hex seven_seg_hex_6 (.d(hexdisplay_1_p13), .dp(hexdisplay_1_p14));
  // fetch fetch_1: pin names not known; wires that end beside it: Program_d, advance_out, R, jump, PC, fetch_1_p6
  Seven_Seg_Hex seven_seg_hex_7 (.d(hexdisplay_1_p15), .dp(hexdisplay_1_p16));
  Seven_Seg_Hex seven_seg_hex_8 (.d(hexdisplay_1_p17), .dp(instrdisplay_1_p1));
  Seven_Seg_Hex seven_seg_hex_9 (.d(instrdisplay_1_p2), .dp(instrdisplay_1_p3));
  Seven_Seg_Hex seven_seg_hex_10 (.d(instrdisplay_1_p4), .dp(instrdisplay_1_p5));
  // decoder decoder_1: pin names not known; wires that end beside it: decoder_1_p1, decoder_1_p2, fetch_1_p6, rs, rd, decoder_1_p6, L, R, tworeg, move, add, op, jump
  SixteenSeg sixteenseg_3 (.led(instrdisplay_1_p6), .dp(instrdisplay_1_p7));
  // instrdisplay instrdisplay_1: pin names not known; wires that end beside it: instrdisplay_1_p1, instrdisplay_1_p2, instrdisplay_1_p3, instrdisplay_1_p4, instrdisplay_1_p5, instrdisplay_1_p6, instrdisplay_1_p7, instrdisplay_1_p8, instrdisplay_1_p9, instrdisplay_1_p10, instrdisplay_1_p11, op, instrdisplay_1_p13, instrdisplay_1_p14, instrdisplay_1_p15, instrdisplay_1_p16, instrdisplay_1_p17, instrdisplay_1_p18
  DipSwitch u_hex (.out(hex));
  SixteenSeg sixteenseg_4 (.led(instrdisplay_1_p8), .dp(instrdisplay_1_p9));
  SixteenSeg sixteenseg_5 (.led(instrdisplay_1_p10), .dp(instrdisplay_1_p11));
  SixteenSeg sixteenseg_6 (.led(instrdisplay_1_p13), .dp(instrdisplay_1_p14));
  SixteenSeg sixteenseg_7 (.led(instrdisplay_1_p15), .dp(instrdisplay_1_p16));
  execute execute_1 (.L(decoder_1_p6), .R(L), .cond(R), .R_out(execute_1_r_out));  // open: op, L_out, result, skip_n
  SixteenSeg sixteenseg_8 (.led(instrdisplay_1_p17), .dp(instrdisplay_1_p18));
  Seven_Seg_Hex seven_seg_hex_11 (.d(hexdisplay_2_p1), .dp(hexdisplay_2_p2));
  Seven_Seg_Hex seven_seg_hex_12 (.d(hexdisplay_2_p3), .dp(hexdisplay_2_p4));
  // hexdisplay hexdisplay_2: pin names not known; wires that end beside it: hexdisplay_2_p1, hexdisplay_2_p2, hexdisplay_2_p3, hexdisplay_2_p4, hexdisplay_2_p5, 1'b1, hexdisplay_2_p7, hexdisplay_2_p8, hexdisplay_2_p9, hexdisplay_2_p10, hexdisplay_2_p11, R, hexdisplay_2_p13, hexdisplay_2_p14, hexdisplay_2_p15, hexdisplay_2_p16, hexdisplay_2_p17, hex
  Seven_Seg_Hex seven_seg_hex_13 (.d(hexdisplay_2_p5), .dp(hexdisplay_2_p7));
  Seven_Seg_Hex seven_seg_hex_14 (.d(hexdisplay_2_p8), .dp(hexdisplay_2_p9));
  // regfile regfile_1: pin names not known; wires that end beside it: rs, rd, execute_1_r_out, advance_out, decoder_1_p1, decoder_1_p2, R0, R1, R2, R3
  Seven_Seg_Hex seven_seg_hex_15 (.d(hexdisplay_2_p10), .dp(hexdisplay_2_p11));
  Seven_Seg_Hex seven_seg_hex_16 (.d(hexdisplay_2_p13), .dp(hexdisplay_2_p14));
  Seven_Seg_Hex seven_seg_hex_17 (.d(hexdisplay_2_p15), .dp(hexdisplay_2_p16));
  Seven_Seg_Hex seven_seg_hex_18 (.d(hexdisplay_2_p17), .dp(regdisplay_2_p1));
  Seven_Seg_Hex seven_seg_hex_19 (.d(regdisplay_2_p2), .dp(regdisplay_2_p3));
  Seven_Seg_Hex seven_seg_hex_20 (.d(regdisplay_2_p4), .dp(regdisplay_2_p5));
  SixteenSeg sixteenseg_9 (.led(regdisplay_2_p6), .dp(regdisplay_2_p8));
  // regdisplay regdisplay_2: pin names not known; wires that end beside it: regdisplay_2_p1, regdisplay_2_p2, regdisplay_2_p3, regdisplay_2_p4, regdisplay_2_p5, regdisplay_2_p6, tworeg, regdisplay_2_p8, 1'b0, regdisplay_2_p10, rs, regdisplay_2_p12
  SixteenSeg sixteenseg_10 (.led(regdisplay_2_p10), .dp(regdisplay_2_p12));

  // Notes on the sheet:
  //   contents of Program (hex, n*v repeats v):
  //   120,61,bd,91,7d,10e
  //   rj45 Creates
endmodule
